# Fritzing sketch ESP32-Relay (saved by Fritzing 0.9.5d)
breadboards: 1

parts:
  ESP32_-_USB_powered = ESP32 DevKitc V4
  5V_relay_-_set_trigger_LOW = 1 chan 5v relay module
  SSD1306_-_3_3V = OLED 128x64 I2C Monochrome Display
  DC_fan_/_motor_load_(~6V) = DC Motor
  GPIO27_reset/start = Round Pushbutton
  R1_10k_upper = Resistor [resistance=10k tolerance=±5% package=THT]
  R2_2_15k_lower = Resistor [resistance=2.15k tolerance=±5% package=THT]
  Shunt_A_10_ohm = Resistor [resistance=10 tolerance=±5% package=THT]
  Shunt_B_10_ohm = Resistor [resistance=10 tolerance=±5% package=THT]
  6V_DC_input_(+_/_GND) = Screw terminal - 2 pins [package=THT]
  Regulated_5V_(+_/_GND) = Screw terminal - 2 pins [package=THT]

nets:
  N1: ESP32_-_USB_powered.Pin_1, SSD1306_-_3_3V.VDD
  N2: ESP32_-_USB_powered.Pin_5, DC_fan_/_motor_load_(~6V).pin_2, Shunt_A_10_ohm.Pin_0, Shunt_B_10_ohm.Pin_0
  N3: ESP32_-_USB_powered.Pin_6, R1_10k_upper.Pin_1, R2_2_15k_lower.Pin_0
  N4: ESP32_-_USB_powered.Pin_10, 5V_relay_-_set_trigger_LOW.pin_3
  N5: ESP32_-_USB_powered.Pin_11, GPIO27_reset/start.leg0
  N6: ESP32_-_USB_powered.Pin_14, ESP32_-_USB_powered.Pin_32, 5V_relay_-_set_trigger_LOW.pin_2, SSD1306_-_3_3V.GND, GPIO27_reset/start.leg1, R2_2_15k_lower.Pin_1, Shunt_A_10_ohm.Pin_1, Shunt_B_10_ohm.Pin_1, 6V_DC_input_(+_/_GND).pin2, Regulated_5V_(+_/_GND).pin2
  N7: ESP32_-_USB_powered.Pin_21, ESP32_-_USB_powered.Pin_33, SSD1306_-_3_3V.SDA
  N8: ESP32_-_USB_powered.Pin_36, SSD1306_-_3_3V.SCK
  N9: 5V_relay_-_set_trigger_LOW.pin_1, Regulated_5V_(+_/_GND).pin1
  N10: 5V_relay_-_set_trigger_LOW.pin_4, DC_fan_/_motor_load_(~6V).pin_1
  N11: 5V_relay_-_set_trigger_LOW.pin_5, R1_10k_upper.Pin_0, 6V_DC_input_(+_/_GND).pin1

notes:
  Educational 6V prototype
  UNPROTECTED ADC INPUTS
  Not for high-power loads
  Verify relay 3.3V logic
  Shunt: 10 ohm || 10 ohm = 5 ohm

custom parts:
  ESP32 DevKitc V4: ESP32-DevKitC board with ESP32-WROOM-32 module. ESP32-DevKitC V4 is a small-sized ESP32-based development board produced by Espressif. Most of the pins on the ESP module are broken out to the pin headers on the board. The pins D0, D1, D2, D3, CMD and CLK are used internally for communication between ESP32 and SPI flash memory. They are grouped on both sides near the USB connector. Avoid using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
  1 chan 5v relay module: 1 Channel 5V Relay Module Board Shield with Optocoupler Support High and Low Level Trigger for Arduino.
